// Logisim project 4inputex2.circ as structural Verilog: 1 circuit, main circuit main
module main (
  input  A,
  input  B,
  input  C,
  input  D,
  output out_5
);

  wire nor_1_out, not_1_out, or_1_out;

  nor nor_1 (nor_1_out, A, B);
  not not_1 (not_1_out, C);
  or or_1 (or_1_out, C, D);
  and and_1 (out_5, nor_1_out, not_1_out, or_1_out);

  // Notes on the sheet:
  //   C+D
  //   (A+B)'
  //   C'
  //   ( (A+B)' C' (C+D) )
endmodule
