// Logisim project 4inputsex3.circ as structural Verilog: 1 circuit, main circuit main
module main (
  input  X,
  input  Y,
  input  Z,
  input  W,
  output out_5
);

  wire and_1_out, and_2_out, not_1_out, not_2_out, or_1_out;

  not not_1 (not_1_out, Y);
  and and_1 (and_1_out, X, not_1_out, Z);
  and and_2 (and_2_out, W, not_1_out);
  or or_1 (or_1_out, and_1_out, W);
  not not_2 (not_2_out, or_1_out);
  or or_2 (out_5, and_1_out, not_2_out, and_2_out);

  // Notes on the sheet:
  //   X.Y'.Z
  //   X.Y'.Z+W
  //   Y'.W
  //   (X.Y'.Z+W)'
  //   X.Y'.Z + ( X.Y'.Z+W)' + Y'.W
endmodule
