// Logisim project 4inputsex4.circ as structural Verilog: 1 circuit, main circuit main
module main (
  input  A,
  input  D,
  input  B,
  input  C,
  output out_5
);

  wire A_prime_out, and_1_out, and_2_out, and_3_out, not_1_out, or_1_out;

  not A_prime (A_prime_out, A);
  not not_1 (not_1_out, D);
  and and_1 (and_1_out, A_prime_out, not_1_out);
  and and_2 (and_2_out, D, B);
  and and_3 (and_3_out, not_1_out, C);
  or or_1 (or_1_out, and_2_out, and_3_out);
  or or_2 (out_5, and_1_out, or_1_out);

  // Notes on the sheet:
  //   D'
  //   A'B'
  //   BD
  //   CD'
  //   BD+CD'
  //   A'B'+BD+CD'
endmodule
