// Logisim project lg2.circ as structural Verilog: 1 circuit, main circuit main
module main (
  input  A,
  input  B,
  input  C,
  output out_4
);

  wire and_1_out, nand_1_out;

  and and_1 (and_1_out, A, B);
  nand nand_1 (nand_1_out, A, C);
  or or_1 (out_4, and_1_out, nand_1_out);

  // Notes on the sheet:
  //   AB
  //   (AC)'
  //   AB+(AC)'
endmodule
