// Logisim project log1.circ as structural Verilog: 1 circuit, main circuit main
module main (
  input  A,
  input  B,
  input  C,
  output out_4
);

  wire AB_out, and_1_out, B_C_out, BC_out;

  and AB (AB_out, A, B);
  or B_C (B_C_out, B, C);
  and BC (BC_out, C, B);
  and and_1 (and_1_out, B_C_out, BC_out);
  or or_1 (out_4, AB_out, and_1_out);

  // Notes on the sheet:
  //   ((B+C)BC)
  //   AB+((B+C)BC)
endmodule
