// Logisim project log3.circ as structural Verilog: 1 circuit, main circuit main
module main (
  input  A,
  input  B,
  output out_3
);

  wire nand_1_out, nand_2_out, or_1_out;

  nand nand_1 (nand_1_out, A, B);
  nand nand_2 (nand_2_out, A, nand_1_out);
  or or_1 (or_1_out, nand_1_out, B);
  nand nand_3 (out_3, nand_2_out, or_1_out);

  // Notes on the sheet:
  //   (AB)'
  //   (AB)'+B
  //   (A(AB)')'
  //   (  ( A (AB)') )'   ((AB)' + B)  )'
endmodule
