// Logisim project log4.circ as structural Verilog: 1 circuit, main circuit main
module main (
  input  A,
  input  B,
  input  C,
  output out_4
);

  wire and_1_out, not_1_out, not_2_out, or_1_out, or_2_out, or_3_out;

  not not_1 (not_1_out, C);
  or or_1 (or_1_out, A, B);
  not not_2 (not_2_out, not_1_out);
  and and_1 (and_1_out, A, not_1_out, B);
  or or_2 (or_2_out, or_1_out, not_2_out);
  or or_3 (or_3_out, not_2_out, and_1_out);
  and and_2 (out_4, or_2_out, or_3_out, and_1_out);

  // Notes on the sheet:
  //   A+B
  //   C''
  //   A.B.C'
  //   A+B+C''
  //   C''+(A.B.C')
  //   ((A+B+C'' ) (C''+ABC' ) (ABC')
endmodule
