// Logisim project log6.circ as structural Verilog: 1 circuit, main circuit main
module main (
  input  A,
  input  B,
  input  C,
  output out_4
);

  wire and_1_out, nand_1_out, not_1_out, not_2_out, not_3_out, or_1_out, xor_1_out;

  not not_1 (not_1_out, C);
  or or_1 (or_1_out, A, B);
  nand nand_1 (nand_1_out, A, B);
  xor xor_1 (xor_1_out, or_1_out, nand_1_out);
  and and_1 (and_1_out, or_1_out, not_1_out);
  not not_2 (not_2_out, xor_1_out);
  not not_3 (not_3_out, and_1_out);
  or or_2 (out_4, not_2_out, not_3_out);

  // Notes on the sheet:
  //   A+B
  //   A'B'
  //   (A+B)+(A'B')
  //   (A+B)C'
endmodule
