// Logisim project abcd.circ as structural Verilog: 1 circuit, main circuit main
module main (
  input  B,
  input  C,
  input  D,
  input  A,
  output w
);

  wire and_1_out, and_2_out, D_prime_out, nand_1_out, nor_1_out, not_1_out, or_1_out, or_2_out;

  not not_1 (not_1_out, B);
  not D_prime (D_prime_out, D);
  nor nor_1 (nor_1_out, not_1_out, D);
  and and_1 (and_1_out, C, C, B);
  or or_1 (or_1_out, not_1_out, D);
  and and_2 (and_2_out, A, D_prime_out);
  or or_2 (or_2_out, nor_1_out, and_1_out);
  nand nand_1 (nand_1_out, or_1_out, and_2_out);
  or or_3 (w, or_2_out, nand_1_out);

  // Notes on the sheet:
  //   B'
  //   (B'+D)'
  //   C.B
  //   B'+D'
  //   A.D'
  //   (B'+D)' +(CB)
  //                   (B'+D') (A.D')'
  //   (B'+D)'+(CB)+(B'+D')(A.D')'
endmodule
