// Logisim project xczxzc.circ as structural Verilog: 1 circuit, main circuit main
module main (
  input  b,
  input  c,
  input  d,
  output w
);

  wire and_1_out, and_2_out, or_1_out;

  and and_1 (and_1_out, b, b, c, d);
  or or_1 (or_1_out, and_1_out, and_1_out, c);
  and and_2 (and_2_out, or_1_out, c, d);
endmodule
