// Logisim project main_circuit.circ as structural Verilog: 1 circuit, main circuit main
module main (
  input  A,
  input  B,
  input  C,
  input  D,
  output out_5
);

  wire and_1_out, and_2_out, D_prime_out, nand_1_out, nor_1_out, or_1_out;

  not D_prime (D_prime_out, D);
  nor nor_1 (nor_1_out, A, B);
  and and_1 (and_1_out, B, D_prime_out);
  nand nand_1 (nand_1_out, C, C, D, D);
  or or_1 (or_1_out, nor_1_out, and_1_out);
  and and_2 (and_2_out, C, nand_1_out);
  or or_2 (out_5, or_1_out, and_2_out);

  // Notes on the sheet:
  //   (A+B)'
  //   B.D'
  //   (CD)'
  //   (A+B)'+B.D'
  //   C.(CD)'
  //      (A+B)' +.B.D' + C(C.D)'
endmodule
